// Logisim project CPU 4BIT.circ as structural Verilog: 4 circuits, main circuit ALU
module ALU (
  input  SUB,
  input  CIN,
  input  [2:0] in_3,
  input  A,
  input  B,
  input  LESS,
  output out_7,
  output COUT,
  output SET
);

  wire and_1_out, nor_1_out, or_1_out, xor_1_out, xor_2_out;

  xor xor_1 (xor_1_out, B, SUB);
  and and_1 (and_1_out, A, B);
  or or_1 (or_1_out, A, B);
  xor xor_2 (xor_2_out, A, B);
  nor nor_1 (nor_1_out, A, B);
  Adder #(.width(1)) adder_1 (.a(A), .b(xor_1_out), .out(SET), .cin(CIN), .cout(COUT));
  Multiplexer #(.select(3)) multiplexer_1 (
    .in0(and_1_out), .in1(or_1_out), .in2(xor_2_out), .in3(nor_1_out), .in4(SET), .in5(LESS), .out(out_7),
    .sel(in_3));  // open: in6, in7, en
endmodule

module CU (
  input  SUB,
  input  [2:0] in_2,
  input  [6:0] in_3,
  input  [6:0] B,
  input  in_5,
  output [6:0] RESULT,
  output ZERO_FLAG,
  output [3:0] out_8,
  output [3:0] out_9
);

  wire alu_1_cout, alu_2_cout, alu_3_cout, alu_4_set;

  ALU alu_1 (
    .A(in_3[0]), .B(B[0]), .out_7(RESULT[0]), .SUB(SUB), .CIN(SUB), .in_3(in_2), .COUT(alu_1_cout),
    .LESS(alu_4_set));  // open: SET
  ALU alu_2 (
    .A(in_3[1]), .B(B[1]), .out_7(RESULT[1]), .SUB(SUB), .CIN(alu_1_cout), .in_3(in_2), .COUT(alu_2_cout),
    .LESS(1'b0));  // open: SET
  ALU alu_3 (
    .A(in_3[2]), .B(B[2]), .out_7(RESULT[2]), .SUB(SUB), .CIN(alu_2_cout), .in_3(in_2), .COUT(alu_3_cout),
    .LESS(1'b0));  // open: SET
  ALU alu_4 (
    .A(in_3[3]), .B(B[3]), .out_7(RESULT[3]), .SUB(SUB), .CIN(alu_3_cout), .in_3(in_2), .LESS(1'b0),
    .SET(alu_4_set));  // open: COUT
  \logic  logic_1 (
    .in_1(in_3), .in_2(B), .in_3(in_5), .out_6(out_8[0]), .out_5(out_8[1]), .out_4(out_8[2]),
    .out_7(out_8[3]), .out_8(out_9));
  nor nor_1 (ZERO_FLAG, RESULT[0], RESULT[1], RESULT[2], RESULT[3]);

  assign RESULT[6:4] = 3'b011;

  // Notes on the sheet:
  //   A
  //   FUNCTION SELECTOR
endmodule

module B (
  input  in_1,
  input  [2:0] in_2,
  output out_3,
  output [3:0] out_4
);

  wire button_1_out, button_2_out, controlled_buffer_1_out, controlled_buffer_2_out, keyboard_1_avail,
       keyboard_2_avail;
  wire [3:0] cu_1_out_9;
  wire [6:0] cu_1_result, keyboard_1_data, keyboard_2_data;

  Button button_1 (.out(button_1_out));
  assign controlled_buffer_1_out = keyboard_1_avail ? button_1_out : 1'bz;  // Controlled_Buffer controlled_buffer_1
  Keyboard keyboard_1 (
    .clk(controlled_buffer_1_out), .avail(keyboard_1_avail), .data(keyboard_1_data));  // open: re, clr
  assign controlled_buffer_2_out = keyboard_2_avail ? button_1_out : 1'bz;  // Controlled_Buffer controlled_buffer_2
  Keyboard keyboard_2 (
    .clk(controlled_buffer_2_out), .avail(keyboard_2_avail), .data(keyboard_2_data));  // open: re, clr
  Button button_2 (.out(button_2_out));
  DotMatrix #(.inputtype("row"), .matrixcols(4), .matrixrows(1)) dotmatrix_1 (.row0(cu_1_out_9));
  CU cu_1 (
    .in_3(keyboard_1_data), .B(keyboard_2_data), .ZERO_FLAG(out_3), .SUB(in_1), .in_2(in_2),
    .RESULT(cu_1_result), .in_5(button_2_out), .out_8(out_4), .out_9(cu_1_out_9));
  TTY tty_1 (.data(cu_1_result), .clk(button_1_out));  // open: we, clr
endmodule

module \logic  (
  input  [6:0] in_1,
  input  [6:0] in_2,
  input  in_3,
  output out_4,
  output out_5,
  output out_6,
  output out_7,
  output [3:0] out_8
);

  wire clock_1_out;
  wire [3:0] counter_1_q;
  wire [6:0] and_1_out;
  wire [6:4] register_1_q;

  Clock clock_1 (.out(clock_1_out));
  Counter #(.width(4), .max('hf)) counter_1 (
    .count(clock_1_out), .Q(counter_1_q), .clk(clock_1_out));  // open: load, D, carry, clr
  assign and_1_out = in_1 & in_2;  // AND_Gate and_1, 7 bits wide
  Register #(.width(7)) register_1 (
    .D(and_1_out), .Q({register_1_q, out_4, out_5, out_6, out_7}), .clk(in_3));  // open: en, clr
  ROM #(.addrWidth(4), .dataWidth(4)) rom_1 (.addr(counter_1_q), .data(out_8));  // open: sel

  // Notes on the sheet:
  //   contents of rom_1 (hex, n*v repeats v):
  //   7 3 1 0 7 3 1 0 7 3 1 0 7 3 1
endmodule
